# Fritzing sketch skripsi_adel (saved by Fritzing 0.9.3b)
circuit board: 7cm x 7cm

parts:
  ESP8266_LOLIN = ESP8266 NodeMCU LoLin module
  MLX90614 = gy-906
  MAX30102 = MakerFocus MAX30102
  OLED_0_96 = OLED 128x64 I2C Monochrome Display
  A1 = j5019
  U2 = LIPO-1000mAh [package=lipo-1000]

nets:
  VIN: ESP8266_LOLIN.3V3, MLX90614.VIN, MAX30102.VIN
  GND: ESP8266_LOLIN.GND, MLX90614.GND, MAX30102.GND, A1.Pin_2, A1.Pin_4, A1.Pin_5, U2.-
  N1: ESP8266_LOLIN.Vin, A1.Pin_1
  N2: MLX90614.SCL, MAX30102.SCL, OLED_0_96.SCK
  N3: MLX90614.SDA, MAX30102.SDA, OLED_0_96.SDA
  N4: A1.Pin_6, U2.+

notes:
  Adelia Azizah Maherani
  11210970000064
  SKRIPSI
  FISIKA INSTRUMENTASI

custom parts:
  ESP8266 NodeMCU LoLin module: ESP8266 based NodeMCU
  gy-906: gy-906 Non-contact PIR I2C interface temperature sensor breakout board.
  MakerFocus MAX30102: Oximeter module using the MAX30102 chip. As usual, if you want the mounting holes in pcb, you need to drag a hole over the pad in silkscreen to actually drill the hole (by default they are not drilled)
  j5019: This module is a small single cell lithium battery charging module which also includes a 1A step-up (boost) converter for powering a large range of applications.
